// Logisim project RV32IDatapath.circ as structural Verilog: 6 circuits, main circuit main
module main (
);

  wire clock_1_out;
  wire [31:0] adder_1_out, adder_2_out, alu_1_p3, alu_2_p3, ALUToReg, EXMEM_q, IDEX_q, IFID_q, immgen_1_p2,
       immgen_2_p2, InstructionMem_data, MemToReg, multiplexer_1_out, multiplexer_2_out, multiplexer_3_out,
       PC_q, ram_1_dout, register_1_q, register_2_q, register_3_q, register_4_q, register_5_q, register_6_q,
       register_7_q, register_8_q, register_11_q, register_12_q, register_13_q, register_14_q, register_16_q;

  Clock clock_1 (.out(clock_1_out));
  Multiplexer #(.width(32)) multiplexer_1 (.in0(adder_2_out), .in1(adder_1_out), .out(multiplexer_1_out));  // open: sel
  Register #(.width(32)) PC (.D(multiplexer_1_out), .clk(clock_1_out), .Q(PC_q));  // open: en, clr
  Adder #(.width(32)) adder_1 (.a(32'h4), .b(PC_q), .out(adder_1_out));  // open: cin, cout
  ROM #(.addrWidth(24), .dataWidth(32)) InstructionMem (.addr(PC_q[23:0]), .data(InstructionMem_data));
  Register #(.width(32)) IFID (.D(PC_q), .clk(clock_1_out), .Q(IFID_q));  // open: en, clr
  Register #(.width(32)) register_1 (.D(InstructionMem_data), .clk(clock_1_out), .Q(register_1_q));  // open: en, clr
  Register #(.width(32)) register_2 (.clk(clock_1_out), .Q(register_2_q));  // open: D, en, clr
  Registers registers_1 (.MemData(MemToReg));
  // ImmGen immgen_1: pin names not known; wires that end beside it: register_1_q, immgen_1_p2
  // ImmGen immgen_2: pin names not known; wires that end beside it: register_2_q, immgen_2_p2
  Adder #(.width(32)) adder_2 (.a(IFID_q), .b(immgen_1_p2), .out(adder_2_out));  // open: cin, cout
  Register #(.width(32)) IDEX (.D(adder_2_out), .clk(clock_1_out), .Q(IDEX_q));  // open: en, clr
  Register #(.width(32)) register_3 (.clk(clock_1_out), .Q(register_3_q));  // open: D, en, clr
  Register #(.width(32)) register_4 (.clk(clock_1_out), .Q(register_4_q));  // open: D, en, clr
  Register #(.width(32)) register_5 (.clk(clock_1_out), .Q(register_5_q));  // open: D, en, clr
  Register #(.width(32)) register_6 (.clk(clock_1_out), .Q(register_6_q));  // open: D, en, clr
  Register #(.width(32)) register_7 (.D(immgen_1_p2), .clk(clock_1_out), .Q(register_7_q));  // open: en, clr
  Register #(.width(32)) register_8 (.D(immgen_2_p2), .clk(clock_1_out), .Q(register_8_q));  // open: en, clr
  Register #(.width(32)) register_9 (.clk(clock_1_out));  // open: D, en, Q, clr
  Register #(.width(32)) register_10 (.clk(clock_1_out));  // open: D, en, Q, clr
  Multiplexer #(.width(32)) multiplexer_2 (.in0(IDEX_q), .in1(register_3_q), .out(multiplexer_2_out));  // open: sel
  Multiplexer #(.width(32)) multiplexer_3 (
    .in0(register_4_q), .in1(register_7_q), .out(multiplexer_3_out));  // open: sel
  // ALU alu_1: pin names not known; wires that end beside it: multiplexer_2_out, multiplexer_3_out, alu_1_p3
  // ALU alu_2: pin names not known; wires that end beside it: register_6_q, register_8_q, alu_2_p3
  Register #(.width(32)) EXMEM (.D(alu_1_p3), .clk(clock_1_out), .Q(EXMEM_q));  // open: en, clr
  Register #(.width(32)) register_11 (.D(register_5_q), .clk(clock_1_out), .Q(register_11_q));  // open: en, clr
  Register #(.width(32)) register_12 (.D(alu_2_p3), .clk(clock_1_out), .Q(register_12_q));  // open: en, clr
  Register #(.width(32)) register_13 (.clk(clock_1_out), .Q(register_13_q));  // open: D, en, clr
  Register #(.width(32)) register_14 (.clk(clock_1_out), .Q(register_14_q));  // open: D, en, clr
  RAM ram_1 (.din(register_11_q[7:0]), .dout(ram_1_dout[7:0]));  // open: addr, we, oe, clk
  Register #(.width(32)) MEM (.D(EXMEM_q), .clk(clock_1_out), .Q(ALUToReg));  // open: en, clr
  Register #(.width(32)) register_15 (.D(ram_1_dout), .clk(clock_1_out), .Q(MemToReg));  // open: en, clr
  Register #(.width(32)) register_16 (.D(register_13_q), .clk(clock_1_out), .Q(register_16_q));  // open: en, clr
  Register #(.width(32)) register_17 (.D(register_14_q), .clk(clock_1_out));  // open: en, Q, clr
  // Pins of 24 and 32 bits meet at PC_q
  // Pins of 8 and 32 bits meet at register_11_q
  // Pins of 8 and 32 bits meet at ram_1_dout
endmodule

module Registers (
  input  [31:0] MemData
);

  wire clock_1_out;

  Clock clock_1 (.out(clock_1_out));
  Register #(.width(32)) x0 (.D(MemData), .clk(clock_1_out));  // open: en, Q, clr
  Register #(.width(32)) x4 (.D(MemData), .clk(clock_1_out));  // open: en, Q, clr
  Register #(.width(32)) x8 (.D(MemData), .clk(clock_1_out));  // open: en, Q, clr
  Register #(.width(32)) x12 (.D(MemData), .clk(clock_1_out));  // open: en, Q, clr
  Register #(.width(32)) x16 (.D(MemData), .clk(clock_1_out));  // open: en, Q, clr
  Register #(.width(32)) x20 (.D(MemData), .clk(clock_1_out));  // open: en, Q, clr
  Register #(.width(32)) x24 (.D(MemData), .clk(clock_1_out));  // open: en, Q, clr
  Register #(.width(32)) x28 (.D(MemData), .clk(clock_1_out));  // open: en, Q, clr
  Register #(.width(32)) x1 (.D(MemData), .clk(clock_1_out));  // open: en, Q, clr
  Register #(.width(32)) x5 (.D(MemData), .clk(clock_1_out));  // open: en, Q, clr
  Register #(.width(32)) x9 (.D(MemData), .clk(clock_1_out));  // open: en, Q, clr
  Register #(.width(32)) x13 (.D(MemData), .clk(clock_1_out));  // open: en, Q, clr
  Register #(.width(32)) x17 (.D(MemData), .clk(clock_1_out));  // open: en, Q, clr
  Register #(.width(32)) x21 (.D(MemData), .clk(clock_1_out));  // open: en, Q, clr
  Register #(.width(32)) x25 (.D(MemData), .clk(clock_1_out));  // open: en, Q, clr
  Register #(.width(32)) x29 (.D(MemData), .clk(clock_1_out));  // open: en, Q, clr
  Register #(.width(32)) x2 (.D(MemData), .clk(clock_1_out));  // open: en, Q, clr
  Register #(.width(32)) x6 (.clk(clock_1_out));  // open: D, en, Q, clr
  Register #(.width(32)) x10 (.D(MemData), .clk(clock_1_out));  // open: en, Q, clr
  Register #(.width(32)) x14 (.D(MemData), .clk(clock_1_out));  // open: en, Q, clr
  Register #(.width(32)) x18 (.D(MemData), .clk(clock_1_out));  // open: en, Q, clr
  Register #(.width(32)) x22 (.D(MemData), .clk(clock_1_out));  // open: en, Q, clr
  Register #(.width(32)) x26 (.D(MemData), .clk(clock_1_out));  // open: en, Q, clr
  Register #(.width(32)) x30 (.D(MemData), .clk(clock_1_out));  // open: en, Q, clr
  Register #(.width(32)) x3 (.D(MemData), .clk(clock_1_out));  // open: en, Q, clr
  Register #(.width(32)) x7 (.D(MemData), .clk(clock_1_out));  // open: en, Q, clr
  Register #(.width(32)) x11 (.D(MemData), .clk(clock_1_out));  // open: en, Q, clr
  Register #(.width(32)) x15 (.D(MemData), .clk(clock_1_out));  // open: en, Q, clr
  Register #(.width(32)) x19 (.D(MemData), .clk(clock_1_out));  // open: en, Q, clr
  Register #(.width(32)) x23 (.D(MemData), .clk(clock_1_out));  // open: en, Q, clr
  Register #(.width(32)) x27 (.D(MemData), .clk(clock_1_out));  // open: en, Q, clr
  Register #(.width(32)) x31 (.D(MemData), .clk(clock_1_out));  // open: en, Q, clr
endmodule

module ALU (
  input  DataA,
  input  DataB,
  output ALUOut
);
endmodule

module ImmGen (
  input  ImmIn,
  output ImmOut
);
endmodule

module ISsplitter (
  input  [31:0] instruction,
  output [6:0] opcode,
  output [4:0] rd,
  output [2:0] funct3,
  output [4:0] rs1,
  output [11:0] imm
);


  assign funct3 = instruction[14:12];
  assign imm = instruction[31:20];
  assign opcode = instruction[6:0];
  assign rd = instruction[11:7];
  assign rs1 = instruction[19:15];
endmodule

module SSsplitter (
  input  [31:0] instruction,
  output [6:0] opcode,
  output [4:0] imm4,
  output [2:0] funct3,
  output [4:0] rs1,
  output [4:0] rs2,
  output [6:0] imm
);


  assign funct3 = instruction[14:12];
  assign imm = instruction[31:25];
  assign imm4 = instruction[11:7];
  assign opcode = instruction[6:0];
  assign rs1 = instruction[19:15];
  assign rs2 = instruction[24:20];
endmodule
